# Fritzing sketch arduino-dojo (saved by Fritzing 0.8.7b)
breadboards: 1

parts:
  Part1 = Arduino Uno (Rev3)
  7_Segment1 = 7 Segment Display
  R1 = Rotary Potentiometer (Small) [maximum_resistance=100kΩ package=THT]
  R2 = Resistor [tolerance=±5% resistance=330 package=THT]
  R3 = Resistor [tolerance=±5% resistance=330 package=THT]
  R4 = Resistor [tolerance=±5% resistance=330 package=THT]
  R5 = Resistor [tolerance=±5% resistance=330 package=THT]
  R6 = Resistor [tolerance=±5% resistance=330 package=THT]
  R7 = Resistor [tolerance=±5% resistance=330 package=THT]
  R8 = Resistor [tolerance=±5% resistance=330 package=THT]
  R9 = Resistor [tolerance=±5% resistance=330 package=THT]

nets:
  N1: Part1.A0, R1.wiper
  N2: Part1.D8, R7.Pin_0
  N3: Part1.D9_PWM, R6.Pin_0
  N4: Part1.D10_PWM/SS, R5.Pin_0
  N5: Part1.D11_PWM/MOSI, R3.Pin_1
  N6: Part1.D12/MISO, R2.Pin_0
  N7: Part1.D13/SCK, R4.Pin_0
  N8: Part1.GND, 7_Segment1.common_cathode#3, 7_Segment1.common_cathode#5, 7_Segment1.common_cathode#11, 7_Segment1.common_cathode#16, R1.leg2
  N9: Part1.D6_PWM, R9.Pin_0
  N10: Part1.D7, R8.Pin_0
  N11: Part1.5V, R1.leg1
  N12: 7_Segment1.Segment_A, R4.Pin_1
  N13: 7_Segment1.Segment_F, R2.Pin_1
  N14: 7_Segment1.Segment_E, R3.Pin_0
  N15: 7_Segment1.Segment_DP, R5.Pin_1
  N16: 7_Segment1.Segment_D, R6.Pin_1
  N17: 7_Segment1.common_cathode#12, R7.Pin_1
  N18: 7_Segment1.Segment_G, R8.Pin_1
  N19: 7_Segment1.Segment_B, R9.Pin_1
