# Fritzing sketch arduino-xxl-rear (saved by Fritzing 0.8.7b)
breadboards: 1

parts:
  7_Segment1 = 7 Segment Display
  Q1 = NPN-Transistor [package="TO92 [THT]"]
  Part1 = Arduino Uno (Rev3)
  R1 = Resistor [tolerance=±1% resistance=1k package=THT]
  Power_plug1 = Power plug
  Q2 = NPN-Transistor [package="TO92 [THT]"]
  Q3 = NPN-Transistor [package="TO92 [THT]"]
  Q4 = NPN-Transistor [package="TO92 [THT]"]
  Q5 = NPN-Transistor [package="TO92 [THT]"]
  Q6 = NPN-Transistor [package="TO92 [THT]"]
  Q7 = NPN-Transistor [package="TO92 [THT]"]
  Q8 = NPN-Transistor [package="TO92 [THT]"]
  R2 = Resistor [tolerance=±1% resistance=1k package=THT]
  R3 = Resistor [tolerance=±1% resistance=1k package=THT]
  R4 = Resistor [tolerance=±1% resistance=1k package=THT]
  R5 = Resistor [tolerance=±1% resistance=1k package=THT]
  R6 = Resistor [tolerance=±1% resistance=1k package=THT]
  R7 = Resistor [tolerance=±1% resistance=1k package=THT]
  R8 = Resistor [tolerance=±1% resistance=1k package=THT]
  R9 = Resistor [tolerance=±1% resistance=330 package=THT]
  R10 = Resistor [tolerance=±1% resistance=330 package=THT]
  R11 = Resistor [tolerance=±1% resistance=330 package=THT]
  R12 = Resistor [tolerance=±1% resistance=470k package=THT]
  R13 = Resistor [tolerance=±1% resistance=330 package=THT]
  R14 = Resistor [tolerance=±1% resistance=330 package=THT]
  R15 = Resistor [tolerance=±1% resistance=330 package=THT]
  R16 = Resistor [tolerance=±1% resistance=330 package=THT]
  R17 = Rotary Potentiometer (Small) [maximum_resistance=100kΩ package=THT]

nets:
  N1: 7_Segment1.Segment_E, R9.Pin_1
  N2: 7_Segment1.Segment_D, R10.Pin_1
  N3: 7_Segment1.Segment_C, R11.Pin_1
  N4: 7_Segment1.Segment_DP, R12.Pin_1
  N5: 7_Segment1.Segment_B, R16.Pin_1
  N6: 7_Segment1.Segment_A, R15.Pin_1
  GND: 7_Segment1.common_anode, Part1.GND, Power_plug1.GND, R17.leg2
  N7: 7_Segment1.Segment_F, R14.Pin_1
  N8: 7_Segment1.Segment_G, R13.Pin_1
  N9: Q1.E, R16.Pin_0
  N10: Q1.B, R1.Pin_0
  VIN: Q1.C, Part1.VIN, Power_plug1.VCC, Q2.C, Q3.C, Q4.C, Q5.C, Q6.C, Q7.C, Q8.C
  N11: Part1.A0, R17.wiper
  N12: Part1.D8, R6.Pin_1
  N13: Part1.D9_PWM, R5.Pin_1
  N14: Part1.D10_PWM/SS, R4.Pin_1
  N15: Part1.D11_PWM/MOSI, R3.Pin_1
  N16: Part1.D12/MISO, R2.Pin_1
  N17: Part1.D13/SCK, R1.Pin_1
  N18: Part1.D6_PWM, R8.Pin_1
  N19: Part1.D7, R7.Pin_1
  N20: Part1.5V, R17.leg1
  N21: Q2.E, R14.Pin_0
  N22: Q2.B, R3.Pin_0
  N23: Q3.E, R15.Pin_0
  N24: Q3.B, R2.Pin_0
  N25: Q4.E, R13.Pin_0
  N26: Q4.B, R4.Pin_0
  N27: Q5.E, R12.Pin_0
  N28: Q5.B, R5.Pin_0
  N29: Q6.E, R11.Pin_0
  N30: Q6.B, R6.Pin_0
  N31: Q7.E, R10.Pin_0
  N32: Q7.B, R7.Pin_0
  N33: Q8.E, R9.Pin_0
  N34: Q8.B, R8.Pin_0
