# Fritzing sketch trafficleds (saved by Fritzing 0.8.7b)
breadboards: 1

parts:
  Raspberry_Pi_B_rev1 = Raspberry Pi B rev2
  LED_-_pin_3 = LED - 5mm [color="Red (633nm)" package="5 mm [THT]"]
  LED_-_pin_5 = LED - 5mm [color="Yellow (595nm)" package="5 mm [THT]"]
  LED_-_pin_7 = LED - 5mm [color="Green (555nm)" package="5 mm [THT]"]
  R1 = Resistor [tolerance=±5% resistance=470 package=THT]
  R2 = Resistor [tolerance=±5% resistance=470 package=THT]
  R3 = Resistor [tolerance=±5% resistance=470 package=THT]

nets:
  N1: Raspberry_Pi_B_rev1.GPIO_2, LED_-_pin_3.anode
  N2: Raspberry_Pi_B_rev1.GPIO_3, LED_-_pin_5.anode
  N3: Raspberry_Pi_B_rev1.GPIO_4, LED_-_pin_7.anode
  N4: Raspberry_Pi_B_rev1.GND, R1.Pin_0, R2.Pin_0, R3.Pin_0
  N5: LED_-_pin_3.cathode, R1.Pin_1
  N6: LED_-_pin_5.cathode, R2.Pin_1
  N7: LED_-_pin_7.cathode, R3.Pin_1
